// Digital circuit jelly-seven.dig as structural Verilog
module jelly_seven (
  input  clock,
  input  halt,
  input  D0,
  input  D1,
  input  D2,
  input  D3,
  input  D4,
  input  D5,
  input  D6,
  input  D7,
  output BOB,
  output one,
  output two,
  output RD,
  output WR,
  output fw,
  output bk,
  output HLT,
  output D0_2,
  output D1_2,
  output D2_2,
  output D3_2,
  output D4_2,
  output D5_2,
  output D6_2,
  output D7_2,
  output A0,
  output A1,
  output A2,
  output A3,
  output A4,
  output A5,
  output A6,
  output A7,
  output ce6,
  output oe4,
  output m2,
  output m1,
  output A8,
  output A9,
  output ce5,
  output oe2,
  output N4,
  output N3,
  output N2,
  output N1
);

  wire not_1_out, U1_p11, U1_p22, u10_2_pin3, u10_2_pin6, u10_2_pin8, u10_2_pin11, u10_2_pin13, u10_2_pin14,
       u10_pin5, u10_pin12, u10_pin13, u11_pin3, u11_pin6;
  wire [7:0] U2_p12, u4_p9, u5_pin19, u6_pin19;
  wire [7:4] u5_pin6;

  LED led_1 (.in(A0));
  PullDown pulldown_1 (.out(A0));
  LED led_2 (.in(A2));
  LED led_3 (.in(A1));
  PullDown pulldown_2 (.out(A1));
  PullDown pulldown_3 (.out(A2));
  LED led_4 (.in(A4));
  LED led_5 (.in(A3));
  PullDown pulldown_4 (.out(A3));
  PullDown pulldown_5 (.out(A4));
  LED led_6 (.in(A6));
  LED led_7 (.in(A5));
  PullDown pulldown_6 (.out(A5));
  PullDown pulldown_7 (.out(A6));
  LED led_8 (.in(A7));
  PullDown pulldown_8 (.out(A7));
  LED led_9 (.in(m1));
  PullDown pulldown_9 (.out(m1));
  LED led_10 (.in(N1));
  PullDown pulldown_10 (.out(N1));
  LED led_11 (.in(oe4));
  LED led_12 (.in(m2));
  PullDown pulldown_11 (.out(m2));
  PullDown pulldown_12 (.out(oe4));
  LED led_13 (.in(N3));
  LED led_14 (.in(N2));
  PullDown pulldown_13 (.out(N2));
  PullDown pulldown_14 (.out(N3));
  LED led_15 (.in(ce6));
  PullDown pulldown_15 (.out(ce6));
  LED led_16 (.in(N4));
  PullDown pulldown_16 (.out(N4));
  _74574 u5 (
    .pin1(ce6), .pin2(m1), .pin3(m2), .pin4(oe4), .pin5(ce6), .pin6(u5_pin6[4]), .pin7(u5_pin6[5]),
    .pin8(u5_pin6[6]), .pin9(u5_pin6[7]), .pin10(ce6), .pin11(ce5), .pin12(u5_pin19[7]), .pin13(u5_pin19[6]),
    .pin14(u5_pin19[5]), .pin15(u5_pin19[4]), .pin16(u5_pin19[3]), .pin17(u5_pin19[2]), .pin18(u5_pin19[1]),
    .pin19(u5_pin19[0]), .pin20(1'b1));
  _74574 u6 (
    .pin1(ce6), .pin2(m1), .pin3(m2), .pin4(oe4), .pin5(ce6), .pin6(u5_pin6[4]), .pin7(u5_pin6[5]),
    .pin8(u5_pin6[6]), .pin9(u5_pin6[7]), .pin10(ce6), .pin11(ce6), .pin12(u6_pin19[7]), .pin13(u6_pin19[6]),
    .pin14(u6_pin19[5]), .pin15(u6_pin19[4]), .pin16(u6_pin19[3]), .pin17(u6_pin19[2]), .pin18(u6_pin19[1]),
    .pin19(u6_pin19[0]), .pin20(1'b1));
  // _28c16 U1: pin names not known; wires that end beside it: A7, A6, A5, A4, A3, A2, A1, A0, m1, m2, U1_p11, ce6, 1'b1, A9, A8, 1'b1, ce6, ce6, ce6, A8, A9, U1_p22
  // _28c16 U2: pin names not known; wires that end beside it: U1_p11, A7, A6, A5, A4, A3, A2, A1, A0, U2_p12[0], U2_p12[1], U2_p12[2], ce6, 1'b1, A9, A8, 1'b1, oe2, ce6, ce6, U2_p12[7], U2_p12[6], U2_p12[5]
  // _28c16 u3: pin names not known; wires that end beside it: u5_pin19[7], u5_pin19[6], u5_pin19[5], u5_pin19[4], u5_pin19[3], u5_pin19[2], u5_pin19[1], u5_pin19[0], N1, N2, N3, ce6, 1'b1, ce6, ce6, 1'b1, ce6, ce6, ce6, A7, A6, A5
  // _28c16 u4: pin names not known; wires that end beside it: u6_pin19[7], u6_pin19[6], u6_pin19[5], u6_pin19[4], u6_pin19[3], u6_pin19[2], u6_pin19[1], u6_pin19[0], u4_p9[0], u4_p9[1], u4_p9[2], ce6, 1'b1, m1, m2, 1'b1, oe4, ce6, ce6, u4_p9[7], u4_p9[6], u4_p9[5]
  LED led_17 (.in(A9));
  LED led_18 (.in(A8));
  PullDown pulldown_17 (.out(A9));
  PullDown pulldown_18 (.out(A8));
  _74574 u7 (
    .pin2(U2_p12[0]), .pin3(U2_p12[1]), .pin4(U2_p12[2]), .pin5(U2_p12[3]), .pin6(U2_p12[4]),
    .pin7(U2_p12[5]), .pin8(U2_p12[6]), .pin9(U2_p12[7]), .pin10(ce6), .pin12(HLT), .pin13(bk), .pin14(fw),
    .pin15(WR), .pin16(RD), .pin17(two), .pin18(one), .pin19(BOB), .pin20(1'b1));  // open: pin1, pin11
  _74574 u8 (
    .pin2(u4_p9[0]), .pin3(u4_p9[1]), .pin4(u4_p9[2]), .pin5(u4_p9[3]), .pin6(u4_p9[4]), .pin7(u4_p9[5]),
    .pin8(u4_p9[6]), .pin9(u4_p9[7]), .pin10(ce6), .pin12(u5_pin6[7]), .pin13(u5_pin6[6]),
    .pin14(u5_pin6[5]), .pin15(u5_pin6[4]), .pin16(ce6), .pin17(oe4), .pin18(m2), .pin19(m1), .pin20(1'b1));  // open: pin1, pin11
  LED led_19 (.in(oe2));
  LED led_20 (.in(ce5));
  PullDown pulldown_19 (.out(oe2));
  PullDown pulldown_20 (.out(ce5));
  LED led_21 (.in(BOB));
  PullDown pulldown_21 (.out(BOB));
  _74193 u10 (
    .pin1(ce6), .pin2(A1), .pin3(A0), .pin4(1'b1), .pin5(u10_pin5), .pin6(A2), .pin7(A3), .pin8(ce6),
    .pin9(ce6), .pin10(ce6), .pin11(1'b1), .pin12(u10_pin12), .pin13(u10_pin13), .pin14(ce5), .pin15(ce6),
    .pin16(1'b1));
  LED led_22 (.in(two));
  LED led_23 (.in(one));
  PullDown pulldown_22 (.out(one));
  PullDown pulldown_23 (.out(two));
  _7432 u10_2 (
    .pin1(u6_pin19[0]), .pin2(u6_pin19[1]), .pin3(u10_2_pin3), .pin4(u6_pin19[2]), .pin5(u6_pin19[3]),
    .pin6(u10_2_pin6), .pin7(1'b0), .pin8(u10_2_pin8), .pin9(u10_2_pin6), .pin10(u10_2_pin3),
    .pin11(u10_2_pin11), .pin12(u10_2_pin8), .pin13(u10_2_pin13), .pin14(u10_2_pin14));
  _7432 u11 (
    .pin1(u6_pin19[4]), .pin2(u6_pin19[5]), .pin3(u11_pin3), .pin4(u6_pin19[6]), .pin5(u6_pin19[7]),
    .pin6(u11_pin6), .pin7(1'b0), .pin8(u10_2_pin13), .pin9(u11_pin6), .pin10(u11_pin3), .pin12(u10_2_pin14),
    .pin13(u10_2_pin14), .pin14(u10_2_pin14));  // open: pin11
  LED led_24 (.in(WR));
  LED led_25 (.in(RD));
  PullDown pulldown_24 (.out(RD));
  PullDown pulldown_25 (.out(WR));
  LED led_26 (.in(bk));
  LED led_27 (.in(fw));
  PullDown pulldown_26 (.out(fw));
  PullDown pulldown_27 (.out(bk));
  LED led_28 (.in(HLT));
  PullDown pulldown_28 (.out(HLT));
  LED led_29 (.in(u10_pin13));
  LED led_30 (.in(u10_pin12));
  LED led_31 (.in(ce5));
  LED led_32 (.in(clock));
  not not_1 (not_1_out, halt);
  LED led_33 (.in(u10_2_pin11));
  LED led_34 (.in(not_1_out));
  and and_1 (u10_pin5, clock, not_1_out);
  LED led_35 (.in(D1));
  LED led_36 (.in(D0));
  PullDown pulldown_29 (.out(D0));
  PullDown pulldown_30 (.out(D1));
  LED led_37 (.in(D3));
  LED led_38 (.in(D2));
  PullDown pulldown_31 (.out(D2));
  PullDown pulldown_32 (.out(D3));
  LED led_39 (.in(D5));
  LED led_40 (.in(D4));
  PullDown pulldown_33 (.out(D4));
  PullDown pulldown_34 (.out(D5));
  LED led_41 (.in(D7));
  LED led_42 (.in(D6));
  PullDown pulldown_35 (.out(D6));
  PullDown pulldown_36 (.out(D7));
  // Pins of 4 and 8 bits meet at {u5_pin6, ce6, oe4, m2, m1}

  assign D0_2 = D0;
  assign D1_2 = D1;
  assign D2_2 = D2;
  assign D3_2 = D3;
  assign D4_2 = D4;
  assign D5_2 = D5;
  assign D6_2 = D6;
  assign D7_2 = D7;
  // also tied to GND on the sheet: ce6

  // Notes on the sheet:
  //   m1, m2, control math operation
  //   oe4 control output enable
  //   cs6 control output enable
  //   Address Bus
  //   Data Bus
  //   FSM Bus
  //   code control eeprom
  //   tape control eeprom
  //   decoder eeprom
  //   lookup math eeprom
  //   A4-A7
  //   A0-A3
  //   Zero detector
  //   pipeline counter
  //   Device Control
endmodule
